# Fritzing sketch Volume Adjustable Keyboard (saved by Fritzing 0.9.3b)
breadboards: 1

parts:
  Part1 = Arduino Uno (Rev3)
  S1 = Pushbutton [package="[THT]"]
  S2 = Pushbutton [package="[THT]"]
  S3 = Pushbutton [package="[THT]"]
  S4 = Pushbutton [package="[THT]"]
  S5 = Pushbutton [package="[THT]"]
  S6 = Pushbutton [package="[THT]"]
  S7 = Pushbutton [package="[THT]"]
  SP1 = SPEAKER [package=pcb_mount_speaker]
  Q1 = TRANSISTOR_NPN [package=to-92-ammo]
  R1 = Resistor [tolerance=±5% resistance=10k package="2010 [SMD]"]
  U1 = POT [package=alps_pot]

nets:
  N1: Part1.D8, S7.Pin_3, S7.Pin_4
  N2: Part1.D13/SCK, R1.Pin_0
  N3: Part1.GND, S1.Pin_1, S1.Pin_2, S2.Pin_1, S2.Pin_2, S3.Pin_1, S3.Pin_2, S4.Pin_1, S4.Pin_2, S5.Pin_1, S5.Pin_2, S6.Pin_1, S6.Pin_2, S7.Pin_1, S7.Pin_2, Q1.E, U1.A
  N4: Part1.D2, S1.Pin_3, S1.Pin_4
  N5: Part1.D3_PWM, S2.Pin_3, S2.Pin_4
  N6: Part1.D4, S5.Pin_3, S5.Pin_4
  N7: Part1.D5_PWM, S3.Pin_3, S3.Pin_4
  N8: Part1.D6_PWM, S4.Pin_3, S4.Pin_4
  N9: Part1.D7, S6.Pin_3, S6.Pin_4
  N10: Part1.5V, U1.E
  N11: SP1.+, U1.S
  N12: SP1.-, Q1.C
  N13: Q1.B, R1.Pin_1

// code stored in the sketch: Volume Adjustable Keyboard.ino
#define cButton 2
#define dButton 3
#define eButton 4
#define fButton 5
#define gButton 6
#define aButton 7
#define bButton 8
#define speakerPin 13

void setup() {
  // put your setup code here, to run once:
  Serial.begin(9600);
  pinMode(aButton,INPUT_PULLUP);
  pinMode(bButton,INPUT_PULLUP);
  pinMode(cButton,INPUT_PULLUP);
  pinMode(dButton,INPUT_PULLUP);
  pinMode(eButton,INPUT_PULLUP);
  pinMode(fButton,INPUT_PULLUP);
  pinMode(gButton,INPUT_PULLUP);
  pinMode(speakerPin,OUTPUT);
}

void loop() {
  // put your main code here, to run repeatedly:
  int aButtonState = digitalRead(aButton);
  int bButtonState = digitalRead(bButton);
  int cButtonState = digitalRead(cButton);
  int dButtonState = digitalRead(dButton);
  int eButtonState = digitalRead(eButton);
  int fButtonState = digitalRead(fButton);
  int gButtonState = digitalRead(gButton);
  if(aButtonState==0){
    noTone(speakerPin);
    tone(speakerPin,440);
    delay(80);
  }
  else if(bButtonState==0){
    noTone(speakerPin);
    tone(speakerPin,493.88);
    delay(80);
  }
  else if(cButtonState==0){
    noTone(speakerPin);
    tone(speakerPin,261.63);
    delay(80);
  }
  else if(dButtonState==0){
    noTone(speakerPin);
    tone(speakerPin,293.66);
    delay(80);
  }
  else if(eButtonState==0){
    noTone(speakerPin);
    tone(speakerPin,329.63);
    delay(80);
  }
  else if(fButtonState==0){
    noTone(speakerPin);
    tone(speakerPin,349.23);
    delay(80);
  }
  else if(gButtonState==0){
    noTone(speakerPin);
    tone(speakerPin,392);
    delay(80);
  }
  delay(20);
  noTone(speakerPin);
}
